// Logisim project UTF-8NISC_SP25_.circ as structural Verilog: 13 circuits, main circuit main
module main (
);

  wire nisc_cpu_1_c, nisc_cpu_1_n, nisc_cpu_1_v, nisc_cpu_1_z;
  wire [3:0] IM_data, IM_data_2, IM_data_3, nisc_cpu_1_im_address_2;
  wire [7:0] nisc_cpu_1_im_address;
  wire [11:0] nisc_cpu_1_or0;

  ROM #(.addrWidth(9), .dataWidth(12)) IM (
    .addr({nisc_cpu_1_im_address_2[0], nisc_cpu_1_im_address}), .data({IM_data_3, IM_data_2, IM_data}));
  NISC_CPU nisc_cpu_1 (
    .IM_Data({IM_data_3, IM_data_2, IM_data}),
    .IM_Address({nisc_cpu_1_im_address_2[0], nisc_cpu_1_im_address}), .N(nisc_cpu_1_n), .Z(nisc_cpu_1_z),
    .C(nisc_cpu_1_c), .V(nisc_cpu_1_v), .OR0(nisc_cpu_1_or0));
  LED led_1 (.in(nisc_cpu_1_n));
  LED led_2 (.in(nisc_cpu_1_z));
  LED led_3 (.in(nisc_cpu_1_c));
  LED led_4 (.in(nisc_cpu_1_v));
  Hex_Digit_Display hex_digit_display_1 (.value(nisc_cpu_1_im_address_2));  // open: dp
  Hex_Digit_Display hex_digit_display_2 (.value(nisc_cpu_1_im_address[7:4]));  // open: dp
  Hex_Digit_Display hex_digit_display_3 (.value(nisc_cpu_1_or0[11:8]));  // open: dp
  Hex_Digit_Display hex_digit_display_4 (.value(nisc_cpu_1_im_address[3:0]));  // open: dp
  Hex_Digit_Display hex_digit_display_5 (.value(IM_data_3));  // open: dp
  Hex_Digit_Display hex_digit_display_6 (.value(nisc_cpu_1_or0[7:4]));  // open: dp
  Hex_Digit_Display hex_digit_display_7 (.value(nisc_cpu_1_or0[3:0]));  // open: dp
  Hex_Digit_Display hex_digit_display_8 (.value(IM_data_2));  // open: dp
  Hex_Digit_Display hex_digit_display_9 (.value(IM_data));  // open: dp

  // Notes on the sheet:
  //   contents of IM (hex, n*v repeats v):
  //   c09 84a 893 81c
  //   NISC
  //   SP25-Example-Demo
  //   IM Address
  //   R0 Contents
  //   IM Data
endmodule

module RegisterFile (
  input  [2:0] RA1,
  input  [2:0] RA2,
  input  [2:0] WA3,
  input  [11:0] WD3,
  input  RegW,
  input  CLK,
  input  Reset,
  output [11:0] RD1,
  output [11:0] RD2,
  output [11:0] OR0
);

  wire decoder_1_out0, decoder_1_out1, decoder_1_out2, decoder_1_out3, decoder_1_out4, decoder_1_out5,
       decoder_1_out6, decoder_1_out7;
  wire [11:0] R1_q, R2_q, R3_q, R4_q, R5_q, R6_q, R7_q;

  Decoder #(.select(3)) decoder_1 (
    .out0(decoder_1_out0), .out1(decoder_1_out1), .out2(decoder_1_out2), .out3(decoder_1_out3),
    .out4(decoder_1_out4), .out5(decoder_1_out5), .out6(decoder_1_out6), .out7(decoder_1_out7), .sel(WA3),
    .en(RegW));
  Register #(.width(12)) R0 (.D(WD3), .en(decoder_1_out0), .clk(CLK), .Q(OR0), .clr(Reset));
  Register #(.width(12)) R1 (.D(WD3), .en(decoder_1_out1), .clk(CLK), .Q(R1_q), .clr(Reset));
  Register #(.width(12)) R2 (.D(WD3), .en(decoder_1_out2), .clk(CLK), .Q(R2_q), .clr(Reset));
  Register #(.width(12)) R3 (.D(WD3), .en(decoder_1_out3), .clk(CLK), .Q(R3_q), .clr(Reset));
  Register #(.width(12)) R4 (.D(WD3), .en(decoder_1_out4), .clk(CLK), .Q(R4_q), .clr(Reset));
  Register #(.width(12)) R5 (.D(WD3), .en(decoder_1_out5), .clk(CLK), .Q(R5_q), .clr(Reset));
  Register #(.width(12)) R6 (.D(WD3), .en(decoder_1_out6), .clk(CLK), .Q(R6_q), .clr(Reset));
  Register #(.width(12)) R7 (.D(WD3), .en(decoder_1_out7), .clk(CLK), .Q(R7_q), .clr(Reset));
  Multiplexer #(.select(3), .width(12)) multiplexer_1 (
    .in0(OR0), .in1(R1_q), .in2(R2_q), .in3(R3_q), .in4(R4_q), .in5(R5_q), .in6(R6_q), .in7(R7_q), .out(RD1),
    .sel(RA1));
  Multiplexer #(.select(3), .width(12)) multiplexer_2 (
    .in0(OR0), .in1(R1_q), .in2(R2_q), .in3(R3_q), .in4(R4_q), .in5(R5_q), .in6(R6_q), .in7(R7_q), .out(RD2),
    .sel(RA2));

  // Notes on the sheet:
  //   000
  //   001
  //   010
  //   011
  //   100
  //   101
  //   110
  //   111
  //   RD1
  //   RD2
endmodule

module ALU (
  input  [11:0] A,
  input  [11:0] B,
  input  [2:0] ALUOP,
  output [11:0] R,
  output N,
  output Z,
  output C,
  output V
);

  wire clas_12bit_1_c_out, not_3_out, not_4_out, not_5_out, xor_1_out, xor_2_out;
  wire [11:0] and_1_out, clas_12bit_1_result, not_1_out, not_2_out, or_1_out, shifter_1_out, shifter_2_out,
       shifter_3_out;

  assign not_1_out = ~A;  // NOT_Gate not_1, 12 bits wide
  Shifter #(.width(12)) shifter_1 (.in(A), .\dist (4'b0001), .out(shifter_1_out));
  Shifter #(.shift("lr"), .width(12)) shifter_2 (.in(A), .\dist (4'b0001), .out(shifter_2_out));
  Shifter #(.shift("ar"), .width(12)) shifter_3 (.in(A), .\dist (4'b0001), .out(shifter_3_out));
  assign and_1_out = A & B;  // AND_Gate and_1, 12 bits wide
  assign or_1_out = A | B;  // OR_Gate or_1, 12 bits wide
  CLAS_12bit clas_12bit_1 (.M(ALUOP[0]), .A(A), .B(B), .c_out(clas_12bit_1_c_out), .result(clas_12bit_1_result));
  Multiplexer #(.select(3), .width(12)) multiplexer_1 (
    .in0(clas_12bit_1_result), .in1(clas_12bit_1_result), .in2(and_1_out), .in3(or_1_out), .in4(not_1_out),
    .in5(shifter_1_out), .in6(shifter_2_out), .in7(shifter_3_out), .out({N, R[10:0]}), .sel(ALUOP));
  assign not_2_out = ~{N, R[10:0]};  // NOT_Gate not_2, 12 bits wide
  ExactlyOne xor_1 (.out(xor_1_out), .in0(A[11]), .in1(ALUOP[0]), .in2(B[11]));
  xor xor_2 (xor_2_out, A[11], N);
  and and_2 (Z, not_2_out[0], not_2_out[1], not_2_out[2], not_2_out[3], not_2_out[4], not_2_out[5], not_2_out[6], not_2_out[7], not_2_out[8], not_2_out[9], not_2_out[10], not_2_out[11]);
  not not_3 (not_3_out, ALUOP[1]);
  not not_4 (not_4_out, xor_1_out);
  not not_5 (not_5_out, ALUOP[1]);
  and and_3 (V, not_4_out, not_5_out, xor_2_out);
  and and_4 (C, clas_12bit_1_c_out, not_3_out);

  assign R[11] = N;

  // Notes on the sheet:
  //   A11
  //   ALUOP_0
  //   B11
  //   ALUOP_1
  //   RMSB
  //   ALUOP_1
endmodule

module NISC_CPU (
  input  [11:0] IM_Data,
  output [8:0] IM_Address,
  output N,
  output Z,
  output C,
  output V,
  output [11:0] OR0
);

  wire alu_1_c, alu_1_n, alu_1_v, alu_1_z, and_1_out, and_2_out, B, CLK, CVW, FlagsW, MOVC, MOVF, not_1_out,
       NZW, RegW, Reset;
  wire [2:0] controlunit_1_aluop, dipswitch_3_p1, PC_q;
  wire [11:0] alu_1_r, clas_12bit_1_result, dipswitch_1_p1, dipswitch_2_p1, flagsreg_1_q12,
       multiplexer_1_out, multiplexer_2_out, multiplexer_3_out, registerfile_1_rd1, registerfile_1_rd2,
       signextend6_1_s12;

  ControlUnit controlunit_1 (
    .IWord(IM_Data), .MOVC(MOVC), .MOVF(MOVF), .RegW(RegW), .FlagsW(FlagsW), .NZW(NZW), .CVW(CVW), .B(B),
    .ALUOP(controlunit_1_aluop));
  RegisterFile registerfile_1 (
    .RA1(IM_Data[5:3]), .RA2(IM_Data[8:6]), .WA3(IM_Data[2:0]), .WD3(multiplexer_3_out), .RegW(RegW),
    .CLK(CLK), .Reset(Reset), .RD1(registerfile_1_rd1), .RD2(registerfile_1_rd2), .OR0(OR0));
  SignExtend6 signextend6_1 (.S6(IM_Data[8:3]), .S12(signextend6_1_s12));
  Hex_Digit_Display hex_digit_display_1 (.value(IM_Data[11:8]));  // open: dp
  Hex_Digit_Display hex_digit_display_2 (.value(IM_Data[7:4]));  // open: dp
  Hex_Digit_Display hex_digit_display_3 (.value(IM_Data[3:0]));  // open: dp
  and and_1 (and_1_out, IM_Data[9], IM_Data[10], IM_Data[11]);
  Multiplexer #(.width(12)) multiplexer_1 (
    .in0(registerfile_1_rd2), .in1(signextend6_1_s12), .out(multiplexer_1_out), .sel(B));
  CLAS_12bit clas_12bit_1 (.A({PC_q, IM_Address}), .B(12'h1), .result(clas_12bit_1_result));  // open: M, c_out
  and and_2 (and_2_out, and_1_out, not_1_out);
  not not_1 (not_1_out, Z);
  Multiplexer #(.width(12)) multiplexer_2 (
    .in0(clas_12bit_1_result), .in1({3'b111, IM_Data[8:0]}), .out(multiplexer_2_out), .sel(and_2_out));
  Hex_Digit_Display hex_digit_display_4 (.value(OR0[11:8]));  // open: dp
  Register #(.width(12)) PC (.D(multiplexer_2_out), .en(CLK), .clk(CLK), .Q({PC_q, IM_Address}), .clr(Reset));
  Clock clock_1 (.out(CLK));
  Button u_Reset (.out(Reset));
  ALU alu_1 (
    .A(registerfile_1_rd1), .B(multiplexer_1_out), .ALUOP(controlunit_1_aluop), .R(alu_1_r), .N(alu_1_n),
    .Z(alu_1_z), .C(alu_1_c), .V(alu_1_v));
  Hex_Digit_Display hex_digit_display_5 (.value(OR0[7:4]));  // open: dp
  Hex_Digit_Display hex_digit_display_6 (.value(OR0[3:0]));  // open: dp
  Hex_Digit_Display hex_digit_display_7 (.value({PC_q, IM_Address[8]}));  // open: dp
  Hex_Digit_Display hex_digit_display_8 (.value(IM_Address[7:4]));  // open: dp
  Hex_Digit_Display hex_digit_display_9 (.value(IM_Address[3:0]));  // open: dp
  FlagsReg flagsreg_1 (
    .N(alu_1_n), .Z(alu_1_z), .C(alu_1_c), .V(alu_1_v), .D12(registerfile_1_rd1), .NZW(NZW), .FlagsW(FlagsW),
    .CVW(CVW), .CLK(CLK), .Reset(Reset), .Nq(N), .Zq(Z), .Cq(C), .Vq(V), .Q12(flagsreg_1_q12));
  LED led_1 (.in(N));
  LED led_2 (.in(Z));
  LED led_3 (.in(C));
  LED led_4 (.in(V));
  Multiplexer #(.select(2), .width(12)) multiplexer_3 (
    .in0(alu_1_r), .in1(signextend6_1_s12), .in2(flagsreg_1_q12), .out(multiplexer_3_out), .sel({MOVF, MOVC}));  // open: in3
  // DipSwitch #(.number(12)) dipswitch_1: pin names not known; wires that end beside it: dipswitch_1_p1
  // DipSwitch #(.number(12)) dipswitch_2: pin names not known; wires that end beside it: dipswitch_2_p1
  // DipSwitch #(.number(3)) dipswitch_3: pin names not known; wires that end beside it: dipswitch_3_p1
  // DipSwitch #(.number(3)) dipswitch_4: pin names not known

  // Notes on the sheet:
  //   BTA
  //   BNZop
  //   PCsrc
  //   isZ
  //   00:ALU
  //   01:MOVC
  //   10:MOVF
endmodule

module SignExtend6 (
  input  [5:0] S6,
  output [11:0] S12
);


  assign S12 = {{7{S6[5]}}, S6[4:0]};
endmodule

module FlagsReg (
  input  N,
  input  Z,
  input  C,
  input  V,
  input  [11:0] D12,
  input  NZW,
  input  FlagsW,
  input  CVW,
  input  CLK,
  input  Reset,
  output Nq,
  output Zq,
  output Cq,
  output Vq,
  output [11:0] Q12
);

  wire [1:0] multiplexer_1_out, multiplexer_2_out;

  Multiplexer #(.width(2)) multiplexer_1 (.in0({V, C}), .in1(D12[1:0]), .out(multiplexer_1_out), .sel(FlagsW));
  Multiplexer #(.width(2)) multiplexer_2 (.in0({Z, N}), .in1(D12[3:2]), .out(multiplexer_2_out), .sel(FlagsW));
  Register #(.width(2)) NZ (.D(multiplexer_2_out), .en(NZW), .clk(CLK), .Q({Q12[1], Nq}), .clr(Reset));
  Register #(.width(2)) CV (.D(multiplexer_1_out), .en(CVW), .clk(CLK), .Q({Q12[3], Cq}), .clr(Reset));

  assign {Q12[11:4], Q12[2], Q12[0]} = {{8{1'b0}}, Cq, Nq};
  assign Vq = Q12[3];
  assign Zq = Q12[1];
endmodule

module ControlUnit (
  input  [11:0] IWord,
  output MOVC,
  output MOVF,
  output RegW,
  output FlagsW,
  output NZW,
  output CVW,
  output B,
  output [2:0] ALUOP
);

  wire and_3_out, and_4_out, comparator_1_eq, comparator_2_eq, comparator_3_eq, comparator_4_eq,
       comparator_5_eq, comparator_6_eq, comparator_7_eq, comparator_8_eq, comparator_9_eq, comparator_10_eq,
       comparator_11_eq, comparator_12_eq, comparator_13_eq, comparator_14_eq, or_1_out, or_3_out, or_4_out;

  Comparator #(.width(3)) comparator_1 (.a(IWord[11:9]), .b(3'b100), .eq(comparator_1_eq));  // open: gt, lt
  Comparator #(.width(3)) comparator_2 (.a(IWord[8:6]), .b(3'b100), .eq(comparator_2_eq));  // open: gt, lt
  Comparator #(.width(3)) comparator_3 (.a(IWord[11:9]), .b(3'b111), .eq(comparator_3_eq));  // open: gt, lt
  Comparator #(.width(3)) comparator_4 (.a(IWord[11:9]), .b(3'b110), .eq(comparator_4_eq));  // open: gt, lt
  Comparator #(.width(3)) comparator_5 (.a(IWord[11:9]), .b(3'b111), .eq(comparator_5_eq));  // open: gt, lt
  Comparator #(.width(3)) comparator_6 (.a(IWord[11:9]), .b(3'b100), .eq(comparator_6_eq));  // open: gt, lt
  Comparator #(.width(3)) comparator_7 (.a(IWord[8:6]), .b(3'b100), .eq(comparator_7_eq));  // open: gt, lt
  Comparator #(.width(3)) comparator_8 (.a(IWord[8:6]), .b(3'b101), .eq(comparator_8_eq));  // open: gt, lt
  Comparator #(.width(3)) comparator_9 (.a(IWord[11:9]), .b(3'b000), .eq(comparator_9_eq));  // open: gt, lt
  Comparator #(.width(3)) comparator_10 (.a(IWord[8:6]), .b(3'b001), .eq(comparator_10_eq));  // open: gt, lt
  Comparator #(.width(3)) comparator_11 (.a(IWord[11:9]), .b(3'b100), .eq(comparator_11_eq));  // open: gt, lt
  Comparator #(.width(3)) comparator_12 (.a(IWord[8:6]), .b(3'b100), .eq(comparator_12_eq));  // open: gt, lt
  Comparator #(.width(3)) comparator_13 (.a(IWord[11:9]), .b(3'b100), .eq(comparator_13_eq));  // open: gt, lt
  Comparator #(.width(3)) comparator_14 (.a(IWord[8:6]), .b(3'b101), .eq(comparator_14_eq));  // open: gt, lt
  Comparator #(.width(3)) comparator_15 (.a(IWord[11:9]), .b(3'b110), .eq(B));  // open: gt, lt
  Multiplexer multiplexer_1 (.in0(IWord[9]), .in1(IWord[6]), .out(ALUOP[0]), .sel(comparator_1_eq));
  Multiplexer multiplexer_2 (.in0(IWord[10]), .in1(IWord[7]), .out(ALUOP[1]), .sel(comparator_1_eq));
  Multiplexer multiplexer_3 (.in0(IWord[11]), .in1(1'b1), .out(ALUOP[2]), .sel(comparator_1_eq));
  or or_1 (or_1_out, comparator_7_eq, comparator_8_eq);
  or or_2 (CVW, comparator_9_eq, comparator_10_eq);
  and and_1 (FlagsW, comparator_11_eq, comparator_12_eq);
  and and_2 (MOVF, comparator_13_eq, comparator_14_eq);
  and and_3 (and_3_out, comparator_1_eq, comparator_2_eq);
  and and_4 (and_4_out, comparator_6_eq, or_1_out);
  or or_3 (or_3_out, and_3_out, comparator_3_eq);
  not not_1 (RegW, or_3_out);
  or or_4 (or_4_out, comparator_4_eq, comparator_5_eq, and_4_out);
  not not_2 (NZW, or_4_out);

  assign MOVC = B;

  // Notes on the sheet:
  //   subOps
  //   Ops
  //   RegW
  //   NZW
  //   CVW
  //   FlagsW
  //   MOVF
endmodule

module MUX_2to1 (
  input  S,
  input  A,
  input  B,
  output Y
);

  wire and_1_out, and_2_out, not_1_out;

  not not_1 (not_1_out, S);
  and and_1 (and_1_out, S, A);
  and and_2 (and_2_out, not_1_out, B);
  or or_1 (Y, and_1_out, and_2_out);
endmodule

module AND_4bit (
  input  [3:0] A,
  input  [3:0] B,
  output [3:0] Y
);

  and and_1 (Y[0], A[0], B[0]);
  and and_2 (Y[1], A[1], B[1]);
  and and_3 (Y[2], A[2], B[2]);
  and and_4 (Y[3], A[3], B[3]);

  // Notes on the sheet:
  //   A: pull=down
  //   B: pull=down
  //   Y: pull=down
endmodule

module BCD_7Seg (
  input  [3:0] in_1,
  output [6:0] out_2
);

  wire bcd_to_7_segment_decoder_1_p1, bcd_to_7_segment_decoder_1_p2, bcd_to_7_segment_decoder_1_p3,
       bcd_to_7_segment_decoder_1_p4, bcd_to_7_segment_decoder_1_p6, bcd_to_7_segment_decoder_1_p7,
       bcd_to_7_segment_decoder_1_p8, comparator_1_gt;

  // BCD_to_7_Segment_decoder bcd_to_7_segment_decoder_1: pin names not known; wires that end beside it: bcd_to_7_segment_decoder_1_p1, bcd_to_7_segment_decoder_1_p2, bcd_to_7_segment_decoder_1_p3, bcd_to_7_segment_decoder_1_p4, in_1, bcd_to_7_segment_decoder_1_p6, bcd_to_7_segment_decoder_1_p7, bcd_to_7_segment_decoder_1_p8
  Comparator #(.mode("unsigned"), .width(4)) comparator_1 (
    .a(in_1), .b(4'b1001), .gt(comparator_1_gt));  // open: eq, lt
  MUX_2to1 a (.S(comparator_1_gt), .A(1'b1), .B(bcd_to_7_segment_decoder_1_p6), .Y(out_2[0]));
  MUX_2to1 b (.S(comparator_1_gt), .A(1'b0), .B(bcd_to_7_segment_decoder_1_p8), .Y(out_2[1]));
  MUX_2to1 c (.S(comparator_1_gt), .A(1'b0), .B(bcd_to_7_segment_decoder_1_p7), .Y(out_2[2]));
  MUX_2to1 d (.S(comparator_1_gt), .A(1'b1), .B(bcd_to_7_segment_decoder_1_p4), .Y(out_2[3]));
  MUX_2to1 e (.S(comparator_1_gt), .A(1'b1), .B(bcd_to_7_segment_decoder_1_p2), .Y(out_2[4]));
  MUX_2to1 f (.S(comparator_1_gt), .A(1'b1), .B(bcd_to_7_segment_decoder_1_p3), .Y(out_2[5]));
  MUX_2to1 g (.S(comparator_1_gt), .A(1'b1), .B(bcd_to_7_segment_decoder_1_p1), .Y(out_2[6]));
  _7_Segment_Display u_7_segment_display_1 (
    .g(out_2[6]), .f(out_2[5]), .a(out_2[0]), .b(out_2[1]), .e(out_2[4]), .d(out_2[3]), .c(out_2[2]));  // open: dp

  // Notes on the sheet:
  //   out_2: pull=down
  //   in_1: pull=down
endmodule

module CLAS_4bit (
  input  M,
  input  c_in,
  input  [3:0] A,
  input  [3:0] B,
  output C_out,
  output out_6,
  output out_7,
  output \output ,
  output out_9
);

  wire and_1_out, and_2_out, and_3_out, and_4_out, and_5_out, and_6_out, and_7_out, and_8_out, and_9_out,
       and_10_out, B0_out, B1_out, B2_out, B3_out, c0_out, c1_out, c2_out, g0_out, g1_out, g2_out, g3_out,
       p0_out, p1_out, p2_out, p3_out;

  xor B3 (B3_out, B[3], M);
  xor B2 (B2_out, B[2], M);
  xor B1 (B1_out, B[1], M);
  xor B0 (B0_out, B[0], M);
  and g3 (g3_out, B3_out, A[3]);
  xor p3 (p3_out, B3_out, A[3]);
  and g2 (g2_out, B2_out, A[2]);
  xor p2 (p2_out, B2_out, A[2]);
  and g1 (g1_out, B1_out, A[1]);
  xor p1 (p1_out, B1_out, A[1]);
  and g0 (g0_out, B0_out, A[0]);
  xor p0 (p0_out, B0_out, A[0]);
  and and_1 (and_1_out, c_in, p0_out, p1_out, p2_out, p3_out);
  and and_2 (and_2_out, g0_out, p1_out, p2_out, p3_out);
  and and_3 (and_3_out, g1_out, p2_out, p3_out);
  and and_4 (and_4_out, g2_out, p3_out);
  and and_5 (and_5_out, p0_out, p1_out, p2_out, c_in);
  and and_6 (and_6_out, g0_out, p1_out, p2_out);
  and and_7 (and_7_out, p2_out, g1_out);
  and and_8 (and_8_out, c_in, p1_out, p0_out);
  and and_9 (and_9_out, g0_out, p1_out);
  and and_10 (and_10_out, c_in, p0_out);
  or c2 (c2_out, g2_out, and_5_out, and_6_out, and_7_out);
  or c1 (c1_out, g1_out, and_8_out, and_9_out);
  or c0 (c0_out, g0_out, and_10_out);
  or c3 (C_out, g3_out, and_1_out, and_2_out, and_3_out, and_4_out);
  xor s3 (out_6, p3_out, c2_out);
  xor s2 (out_7, p2_out, c1_out);
  xor s1 (\output , p1_out, c0_out);
  xor s0 (out_9, p0_out, c_in);

  // Notes on the sheet:
  //   A: pull=down
  //   B: pull=down
  //   M: pull=down
  //   c_in: pull=down
  //   C_out: pull=down
  //   out_6: pull=down
  //   out_7: pull=down
  //   output: pull=down
  //   out_9: pull=down
  //   c_in
endmodule

module CLAS_12bit (
  input  M,
  input  [11:0] A,
  input  [11:0] B,
  output c_out,
  output [11:0] result
);

  wire clas_4bit_1_c_out, clas_4bit_2_c_out;

  CLAS_4bit clas_4bit_1 (
    .M(M), .c_in(M), .A(A[3:0]), .B(B[3:0]), .C_out(clas_4bit_1_c_out), .out_6(result[3]), .out_7(result[2]),
    .\output (result[1]), .out_9(result[0]));
  CLAS_4bit clas_4bit_2 (
    .M(M), .c_in(clas_4bit_1_c_out), .A(A[7:4]), .B(B[7:4]), .C_out(clas_4bit_2_c_out), .out_6(result[7]),
    .out_7(result[6]), .\output (result[5]), .out_9(result[4]));
  CLAS_4bit clas_4bit_3 (
    .M(M), .c_in(clas_4bit_2_c_out), .A(A[11:8]), .B(B[11:8]), .C_out(c_out), .out_6(result[11]),
    .out_7(result[10]), .\output (result[9]), .out_9(result[8]));

  // Notes on the sheet:
  //   result: pull=down
  //   c_out: pull=down
  //   M: pull=down
  //   A: pull=down
  //   B: pull=down
  //   A0-A3/B0-B3
  //   A4-A7/B4-B7
  //   A8-A11/B8-B11
  //   2048 1024 512 256
  //   128 64 32 16
  //   8 4 2 1
endmodule

module ALU_12bit (
  input  [2:0] OpCode,
  input  [11:0] B,
  input  [11:0] A,
  output V,
  output Z,
  output C,
  output N,
  output [11:0] Sum
);

  wire not_2_out, not_3_out, xor_1_out, xor_2_out;
  wire [11:0] and_1_out, clas_12bit_1_result, not_1_out, or_1_out;

  assign and_1_out = B & A;  // AND_Gate and_1, 12 bits wide
  assign or_1_out = B | A;  // OR_Gate or_1, 12 bits wide
  assign not_1_out = ~A;  // NOT_Gate not_1, 12 bits wide
  CLAS_12bit clas_12bit_1 (.M(OpCode[0]), .A(A), .B(B), .c_out(C), .result(clas_12bit_1_result));
  not not_2 (not_2_out, xor_1_out);
  ExactlyOne xor_1 (.out(xor_1_out), .in0(B[11]), .in1(OpCode[0]), .in2(A[11]));
  and and_2 (V, not_2_out, not_3_out, xor_2_out);
  xor xor_2 (xor_2_out, A[11], N);
  not not_3 (not_3_out, OpCode[1]);
  and and_3 (Z, N, Sum[10], Sum[9], Sum[8], Sum[7], Sum[6], Sum[5], Sum[4], Sum[3], Sum[2], Sum[1], Sum[0]);
  Multiplexer #(.select(3), .width(12)) multiplexer_1 (
    .in0(clas_12bit_1_result), .in1(clas_12bit_1_result), .in2(and_1_out), .in3(or_1_out), .in4(not_1_out),
    .out({N, Sum[10:0]}), .sel(OpCode));  // open: in5, in6, in7
  LED led_1 (.in(N));
  LED led_2 (.in(Sum[10]));
  LED led_3 (.in(Sum[9]));
  LED led_4 (.in(Sum[8]));
  LED led_5 (.in(Sum[7]));
  LED led_6 (.in(Sum[6]));
  LED led_7 (.in(Sum[5]));
  LED led_8 (.in(Sum[4]));
  LED led_9 (.in(Sum[3]));
  LED led_10 (.in(Sum[2]));
  LED led_11 (.in(Sum[1]));
  LED led_12 (.in(Sum[0]));

  assign Sum[11] = N;

  // Notes on the sheet:
  //   B: pull=down
  //   A: pull=down
  //   OpCode: pull=down
  //   V: pull=down
  //   Z: pull=down
  //   C: pull=down
  //   N: pull=down
  //   Sum: pull=down
  //   B11
  //   A11
endmodule
