// Logisim project HW2_1.circ as structural Verilog: 1 circuit, main circuit main
module main (
);

  wire ABCD_sw1, ABCD_sw2, ABCD_sw3, ABCD_sw4, and_1_out, and_2_out, and_3_out, and_4_out, and_5_out,
       and_6_out, and_7_out, and_8_out, and_9_out, not_1_out, not_2_out, not_3_out, not_4_out, or_1_out,
       or_2_out;

  not not_1 (not_1_out, ABCD_sw1);
  not not_2 (not_2_out, ABCD_sw2);
  not not_3 (not_3_out, ABCD_sw3);
  not not_4 (not_4_out, ABCD_sw4);
  DipSwitch #(.number(4)) ABCD (.sw1(ABCD_sw1), .sw2(ABCD_sw2), .sw3(ABCD_sw3), .sw4(ABCD_sw4));
  and and_1 (and_1_out, not_1_out, not_2_out, ABCD_sw3, ABCD_sw4);
  and and_2 (and_2_out, not_1_out, ABCD_sw2, ABCD_sw2, not_4_out);
  and and_3 (and_3_out, ABCD_sw1, not_2_out, not_3_out, ABCD_sw4);
  and and_4 (and_4_out, ABCD_sw1, ABCD_sw2, not_3_out, not_4_out);
  and and_5 (and_5_out, ABCD_sw1, ABCD_sw2, ABCD_sw3, ABCD_sw4);
  and and_6 (and_6_out, ABCD_sw2, not_3_out, ABCD_sw4);
  and and_7 (and_7_out, not_1_out, ABCD_sw2, ABCD_sw4);
  and and_8 (and_8_out, not_2_out, ABCD_sw3, ABCD_sw4);
  and and_9 (and_9_out, not_1_out, not_1_out, ABCD_sw4);
  or or_1 (or_1_out, and_1_out, and_2_out, and_3_out, and_4_out, and_5_out);
  or or_2 (or_2_out, and_6_out, and_7_out, and_8_out, and_9_out);
  LED D (.in(or_1_out));
  LED P (.in(or_2_out));
endmodule
