// Logisim project HW2_2.circ as structural Verilog: 2 circuits, main circuit main
module MUX_2to1 (
  input  S,
  input  A,
  input  B,
  output Y
);

  wire and_1_out, and_2_out, not_1_out;

  not not_1 (not_1_out, S);
  and and_1 (and_1_out, S, A);
  and and_2 (and_2_out, not_1_out, B);
  or or_1 (Y, and_1_out, and_2_out);
endmodule

module main (
);

  wire mux_2to1_1_y, SAB_sw1, SAB_sw2, SAB_sw3;

  DipSwitch #(.number(3)) SAB (.sw1(SAB_sw1), .sw2(SAB_sw2), .sw3(SAB_sw3));
  LED led_1 (.in(mux_2to1_1_y));
  MUX_2to1 mux_2to1_1 (.S(SAB_sw1), .A(SAB_sw2), .B(SAB_sw3), .Y(mux_2to1_1_y));
endmodule
