// Logisim project HW2_4.circ as structural Verilog
module MUX_2to1 (
  input  S,
  input  A,
  input  B,
  output Y
);

  wire and_1_out, and_2_out, not_1_out;

  not not_1 (not_1_out, S);
  and and_1 (and_1_out, S, A);
  and and_2 (and_2_out, not_1_out, B);
  or or_1 (Y, and_1_out, and_2_out);
endmodule

module AND_4bit (
  input  [3:0] A,
  input  [3:0] B,
  output [3:0] Y
);

  and and_1 (Y[0], A[0], B[0]);
  and and_2 (Y[1], A[1], B[1]);
  and and_3 (Y[2], A[2], B[2]);
  and and_4 (Y[3], A[3], B[3]);

  // Notes on the sheet:
  //   A: pull=down
  //   B: pull=down
  //   Y: pull=down
endmodule

module BCD_7Seg (
  input  [3:0] in_1,
  output [6:0] out_2
);

  wire bcd_to_7_segment_decoder_1_p1, bcd_to_7_segment_decoder_1_p2, bcd_to_7_segment_decoder_1_p3,
       bcd_to_7_segment_decoder_1_p4, bcd_to_7_segment_decoder_1_p6, bcd_to_7_segment_decoder_1_p7,
       bcd_to_7_segment_decoder_1_p8, comparator_1_gt;

  // BCD_to_7_Segment_decoder bcd_to_7_segment_decoder_1: pin names not known; wires that end beside it: bcd_to_7_segment_decoder_1_p1, bcd_to_7_segment_decoder_1_p2, bcd_to_7_segment_decoder_1_p3, bcd_to_7_segment_decoder_1_p4, in_1, bcd_to_7_segment_decoder_1_p6, bcd_to_7_segment_decoder_1_p7, bcd_to_7_segment_decoder_1_p8
  Comparator #(.mode("unsigned"), .width(4)) comparator_1 (
    .a(in_1), .b(4'b1001), .gt(comparator_1_gt));  // open: eq, lt
  MUX_2to1 a (.S(comparator_1_gt), .A(1'b1), .B(bcd_to_7_segment_decoder_1_p6), .Y(out_2[0]));
  MUX_2to1 b (.S(comparator_1_gt), .A(1'b0), .B(bcd_to_7_segment_decoder_1_p8), .Y(out_2[1]));
  MUX_2to1 c (.S(comparator_1_gt), .A(1'b0), .B(bcd_to_7_segment_decoder_1_p7), .Y(out_2[2]));
  MUX_2to1 d (.S(comparator_1_gt), .A(1'b1), .B(bcd_to_7_segment_decoder_1_p4), .Y(out_2[3]));
  MUX_2to1 e (.S(comparator_1_gt), .A(1'b1), .B(bcd_to_7_segment_decoder_1_p2), .Y(out_2[4]));
  MUX_2to1 f (.S(comparator_1_gt), .A(1'b1), .B(bcd_to_7_segment_decoder_1_p3), .Y(out_2[5]));
  MUX_2to1 g (.S(comparator_1_gt), .A(1'b1), .B(bcd_to_7_segment_decoder_1_p1), .Y(out_2[6]));
  _7_Segment_Display u_7_segment_display_1 (
    .g(out_2[6]), .f(out_2[5]), .a(out_2[0]), .b(out_2[1]), .e(out_2[4]), .d(out_2[3]), .c(out_2[2]));  // open: dp

  // Notes on the sheet:
  //   out_2: pull=down
  //   in_1: pull=down
endmodule
