// Logisim project HW2_5.circ as structural Verilog: 4 circuits, main circuit main
module MUX_2to1 (
  input  S,
  input  A,
  input  B,
  output Y
);

  wire and_1_out, and_2_out, not_1_out;

  not not_1 (not_1_out, S);
  and and_1 (and_1_out, S, A);
  and and_2 (and_2_out, not_1_out, B);
  or or_1 (Y, and_1_out, and_2_out);
endmodule

module main (
);

  wire A_sw1, A_sw2, A_sw3, A_sw4, and_1_out, and_2_out, and_3_out, and_4_out, and_5_out, and_6_out,
       and_7_out, and_8_out, and_9_out, and_10_out, B0_out, B1_out, B2_out, B3_out, B_sw1, B_sw2, B_sw3,
       B_sw4, c0_out, c1_out, c2_out, c3_out, g0_out, g1_out, g2_out, g3_out, M_sw1, p0_out, p1_out, p2_out,
       p3_out, s0_out, s1_out, s2_out, s3_out;

  DipSwitch #(.number(4)) A (.sw1(A_sw1), .sw2(A_sw2), .sw3(A_sw3), .sw4(A_sw4));
  xor B0 (B0_out, B_sw1, M_sw1);
  DipSwitch #(.number(4)) B (.sw1(B_sw1), .sw2(B_sw2), .sw3(B_sw3), .sw4(B_sw4));
  xor B1 (B1_out, B_sw2, M_sw1);
  DipSwitch #(.number(4)) M (.sw1(M_sw1));  // open: sw2, sw3, sw4
  xor B2 (B2_out, B_sw3, M_sw1);
  xor B3 (B3_out, B_sw4, M_sw1);
  and g3 (g3_out, B3_out, A_sw4);
  xor p3 (p3_out, B3_out, A_sw4);
  and g2 (g2_out, B2_out, A_sw3);
  xor p2 (p2_out, B2_out, A_sw3);
  and g1 (g1_out, B1_out, A_sw2);
  xor p1 (p1_out, B1_out, A_sw2);
  and g0 (g0_out, B0_out, A_sw1);
  xor p0 (p0_out, B0_out, A_sw1);
  and and_1 (and_1_out, M_sw1, p0_out, p1_out, p2_out, p3_out);
  and and_2 (and_2_out, g0_out, p1_out, p2_out, p3_out);
  and and_3 (and_3_out, g1_out, p2_out, p3_out);
  and and_4 (and_4_out, g2_out, p3_out);
  and and_5 (and_5_out, p0_out, p1_out, p2_out, M_sw1);
  and and_6 (and_6_out, g0_out, p1_out, p2_out);
  and and_7 (and_7_out, p2_out, g1_out);
  and and_8 (and_8_out, M_sw1, p1_out, p0_out);
  and and_9 (and_9_out, g0_out, p1_out);
  and and_10 (and_10_out, M_sw1, p0_out);
  or c2 (c2_out, g2_out, and_5_out, and_6_out, and_7_out);
  or c1 (c1_out, g1_out, and_8_out, and_9_out);
  or c0 (c0_out, g0_out, and_10_out);
  or c3 (c3_out, g3_out, and_1_out, and_2_out, and_3_out, and_4_out);
  xor s3 (s3_out, p3_out, c2_out);
  xor s2 (s2_out, p2_out, c1_out);
  xor s1 (s1_out, p1_out, c0_out);
  xor s0 (s0_out, p0_out, M_sw1);
  LED led_1 (.in(c3_out));
  LED led_2 (.in(s3_out));
  LED led_3 (.in(s2_out));
  LED led_4 (.in(s1_out));
  LED led_5 (.in(s0_out));

  // Notes on the sheet:
  //   c_in
  //   C_out
  //   output
endmodule

module AND_4bit (
  input  [3:0] A,
  input  [3:0] B,
  output [3:0] Y
);

  and and_1 (Y[0], A[0], B[0]);
  and and_2 (Y[1], A[1], B[1]);
  and and_3 (Y[2], A[2], B[2]);
  and and_4 (Y[3], A[3], B[3]);

  // Notes on the sheet:
  //   A: pull=down
  //   B: pull=down
  //   Y: pull=down
endmodule

module BCD_7Seg (
  input  [3:0] in_1,
  output [6:0] out_2
);

  wire bcd_to_7_segment_decoder_1_p1, bcd_to_7_segment_decoder_1_p2, bcd_to_7_segment_decoder_1_p3,
       bcd_to_7_segment_decoder_1_p4, bcd_to_7_segment_decoder_1_p6, bcd_to_7_segment_decoder_1_p7,
       bcd_to_7_segment_decoder_1_p8, comparator_1_gt;

  // BCD_to_7_Segment_decoder bcd_to_7_segment_decoder_1: pin names not known; wires that end beside it: bcd_to_7_segment_decoder_1_p1, bcd_to_7_segment_decoder_1_p2, bcd_to_7_segment_decoder_1_p3, bcd_to_7_segment_decoder_1_p4, in_1, bcd_to_7_segment_decoder_1_p6, bcd_to_7_segment_decoder_1_p7, bcd_to_7_segment_decoder_1_p8
  Comparator #(.mode("unsigned"), .width(4)) comparator_1 (
    .a(in_1), .b(4'b1001), .gt(comparator_1_gt));  // open: eq, lt
  MUX_2to1 a (.S(comparator_1_gt), .A(1'b1), .B(bcd_to_7_segment_decoder_1_p6), .Y(out_2[0]));
  MUX_2to1 b (.S(comparator_1_gt), .A(1'b0), .B(bcd_to_7_segment_decoder_1_p8), .Y(out_2[1]));
  MUX_2to1 c (.S(comparator_1_gt), .A(1'b0), .B(bcd_to_7_segment_decoder_1_p7), .Y(out_2[2]));
  MUX_2to1 d (.S(comparator_1_gt), .A(1'b1), .B(bcd_to_7_segment_decoder_1_p4), .Y(out_2[3]));
  MUX_2to1 e (.S(comparator_1_gt), .A(1'b1), .B(bcd_to_7_segment_decoder_1_p2), .Y(out_2[4]));
  MUX_2to1 f (.S(comparator_1_gt), .A(1'b1), .B(bcd_to_7_segment_decoder_1_p3), .Y(out_2[5]));
  MUX_2to1 g (.S(comparator_1_gt), .A(1'b1), .B(bcd_to_7_segment_decoder_1_p1), .Y(out_2[6]));
  _7_Segment_Display u_7_segment_display_1 (
    .g(out_2[6]), .f(out_2[5]), .a(out_2[0]), .b(out_2[1]), .e(out_2[4]), .d(out_2[3]), .c(out_2[2]));  // open: dp

  // Notes on the sheet:
  //   out_2: pull=down
  //   in_1: pull=down
endmodule
