// Logisim project HW4_2.circ as structural Verilog: 5 circuits, main circuit main
module MUX_2to1 (
  input  S,
  input  A,
  input  B,
  output Y
);

  wire and_1_out, and_2_out, not_1_out;

  not not_1 (not_1_out, S);
  and and_1 (and_1_out, S, A);
  and and_2 (and_2_out, not_1_out, B);
  or or_1 (Y, and_1_out, and_2_out);
endmodule

module main (
  input  M,
  input  [11:0] A,
  input  [11:0] B
);

  wire clas_4bit_1_c_out, clas_4bit_1_out_6, clas_4bit_1_out_7, clas_4bit_1_out_9, clas_4bit_1_output,
       clas_4bit_2_c_out, clas_4bit_2_out_6, clas_4bit_2_out_7, clas_4bit_2_out_9, clas_4bit_2_output,
       clas_4bit_3_c_out, clas_4bit_3_out_6, clas_4bit_3_out_7, clas_4bit_3_out_9, clas_4bit_3_output;

  CLAS_4bit clas_4bit_1 (
    .M(M), .c_in(M), .A(A[3:0]), .B(B[3:0]), .C_out(clas_4bit_1_c_out), .out_6(clas_4bit_1_out_6),
    .out_7(clas_4bit_1_out_7), .\output (clas_4bit_1_output), .out_9(clas_4bit_1_out_9));
  CLAS_4bit clas_4bit_2 (
    .M(M), .c_in(clas_4bit_1_c_out), .A(A[7:4]), .B(B[7:4]), .C_out(clas_4bit_2_c_out),
    .out_6(clas_4bit_2_out_6), .out_7(clas_4bit_2_out_7), .\output (clas_4bit_2_output),
    .out_9(clas_4bit_2_out_9));
  CLAS_4bit clas_4bit_3 (
    .M(M), .c_in(clas_4bit_2_c_out), .A(A[11:8]), .B(B[11:8]), .C_out(clas_4bit_3_c_out),
    .out_6(clas_4bit_3_out_6), .out_7(clas_4bit_3_out_7), .\output (clas_4bit_3_output),
    .out_9(clas_4bit_3_out_9));
  LED C_out (.in(clas_4bit_3_c_out));
  LED led_1 (.in(clas_4bit_3_out_6));
  LED led_2 (.in(clas_4bit_3_out_7));
  LED led_3 (.in(clas_4bit_3_output));
  LED led_4 (.in(clas_4bit_3_out_9));
  LED led_5 (.in(clas_4bit_2_out_6));
  LED led_6 (.in(clas_4bit_2_out_7));
  LED led_7 (.in(clas_4bit_2_output));
  LED led_8 (.in(clas_4bit_2_out_9));
  LED led_9 (.in(clas_4bit_1_out_6));
  LED led_10 (.in(clas_4bit_1_out_7));
  LED led_11 (.in(clas_4bit_1_output));
  LED led_12 (.in(clas_4bit_1_out_9));

  // Notes on the sheet:
  //   M: pull=down
  //   A: pull=down
  //   B: pull=down
  //   A0-A3/B0-B3
  //   A4-A7/B4-B7
  //   A8-A11/B8-B11
  //   2048 1024 512 256
  //   128 64 32 16
  //   8 4 2 1
endmodule

module AND_4bit (
  input  [3:0] A,
  input  [3:0] B,
  output [3:0] Y
);

  and and_1 (Y[0], A[0], B[0]);
  and and_2 (Y[1], A[1], B[1]);
  and and_3 (Y[2], A[2], B[2]);
  and and_4 (Y[3], A[3], B[3]);

  // Notes on the sheet:
  //   A: pull=down
  //   B: pull=down
  //   Y: pull=down
endmodule

module BCD_7Seg (
  input  [3:0] in_1,
  output [6:0] out_2
);

  wire bcd_to_7_segment_decoder_1_p1, bcd_to_7_segment_decoder_1_p2, bcd_to_7_segment_decoder_1_p3,
       bcd_to_7_segment_decoder_1_p4, bcd_to_7_segment_decoder_1_p6, bcd_to_7_segment_decoder_1_p7,
       bcd_to_7_segment_decoder_1_p8, comparator_1_gt;

  // BCD_to_7_Segment_decoder bcd_to_7_segment_decoder_1: pin names not known; wires that end beside it: bcd_to_7_segment_decoder_1_p1, bcd_to_7_segment_decoder_1_p2, bcd_to_7_segment_decoder_1_p3, bcd_to_7_segment_decoder_1_p4, in_1, bcd_to_7_segment_decoder_1_p6, bcd_to_7_segment_decoder_1_p7, bcd_to_7_segment_decoder_1_p8
  Comparator #(.mode("unsigned"), .width(4)) comparator_1 (
    .a(in_1), .b(4'b1001), .gt(comparator_1_gt));  // open: eq, lt
  MUX_2to1 a (.S(comparator_1_gt), .A(1'b1), .B(bcd_to_7_segment_decoder_1_p6), .Y(out_2[0]));
  MUX_2to1 b (.S(comparator_1_gt), .A(1'b0), .B(bcd_to_7_segment_decoder_1_p8), .Y(out_2[1]));
  MUX_2to1 c (.S(comparator_1_gt), .A(1'b0), .B(bcd_to_7_segment_decoder_1_p7), .Y(out_2[2]));
  MUX_2to1 d (.S(comparator_1_gt), .A(1'b1), .B(bcd_to_7_segment_decoder_1_p4), .Y(out_2[3]));
  MUX_2to1 e (.S(comparator_1_gt), .A(1'b1), .B(bcd_to_7_segment_decoder_1_p2), .Y(out_2[4]));
  MUX_2to1 f (.S(comparator_1_gt), .A(1'b1), .B(bcd_to_7_segment_decoder_1_p3), .Y(out_2[5]));
  MUX_2to1 g (.S(comparator_1_gt), .A(1'b1), .B(bcd_to_7_segment_decoder_1_p1), .Y(out_2[6]));
  _7_Segment_Display u_7_segment_display_1 (
    .g(out_2[6]), .f(out_2[5]), .a(out_2[0]), .b(out_2[1]), .e(out_2[4]), .d(out_2[3]), .c(out_2[2]));  // open: dp

  // Notes on the sheet:
  //   out_2: pull=down
  //   in_1: pull=down
endmodule

module CLAS_4bit (
  input  M,
  input  c_in,
  input  [3:0] A,
  input  [3:0] B,
  output C_out,
  output out_6,
  output out_7,
  output \output ,
  output out_9
);

  wire and_1_out, and_2_out, and_3_out, and_4_out, and_5_out, and_6_out, and_7_out, and_8_out, and_9_out,
       and_10_out, B0_out, B1_out, B2_out, B3_out, c0_out, c1_out, c2_out, g0_out, g1_out, g2_out, g3_out,
       p0_out, p1_out, p2_out, p3_out;

  xor B3 (B3_out, B[3], M);
  xor B2 (B2_out, B[2], M);
  xor B1 (B1_out, B[1], M);
  xor B0 (B0_out, B[0], M);
  and g3 (g3_out, B3_out, A[3]);
  xor p3 (p3_out, B3_out, A[3]);
  and g2 (g2_out, B2_out, A[2]);
  xor p2 (p2_out, B2_out, A[2]);
  and g1 (g1_out, B1_out, A[1]);
  xor p1 (p1_out, B1_out, A[1]);
  and g0 (g0_out, B0_out, A[0]);
  xor p0 (p0_out, B0_out, A[0]);
  and and_1 (and_1_out, c_in, p0_out, p1_out, p2_out, p3_out);
  and and_2 (and_2_out, g0_out, p1_out, p2_out, p3_out);
  and and_3 (and_3_out, g1_out, p2_out, p3_out);
  and and_4 (and_4_out, g2_out, p3_out);
  and and_5 (and_5_out, p0_out, p1_out, p2_out, c_in);
  and and_6 (and_6_out, g0_out, p1_out, p2_out);
  and and_7 (and_7_out, p2_out, g1_out);
  and and_8 (and_8_out, c_in, p1_out, p0_out);
  and and_9 (and_9_out, g0_out, p1_out);
  and and_10 (and_10_out, c_in, p0_out);
  or c2 (c2_out, g2_out, and_5_out, and_6_out, and_7_out);
  or c1 (c1_out, g1_out, and_8_out, and_9_out);
  or c0 (c0_out, g0_out, and_10_out);
  or c3 (C_out, g3_out, and_1_out, and_2_out, and_3_out, and_4_out);
  xor s3 (out_6, p3_out, c2_out);
  xor s2 (out_7, p2_out, c1_out);
  xor s1 (\output , p1_out, c0_out);
  xor s0 (out_9, p0_out, c_in);

  // Notes on the sheet:
  //   A: pull=down
  //   B: pull=down
  //   M: pull=down
  //   c_in: pull=down
  //   C_out: pull=down
  //   out_6: pull=down
  //   out_7: pull=down
  //   output: pull=down
  //   out_9: pull=down
  //   c_in
endmodule
