// Logisim project HW4_3.circ as structural Verilog: 6 circuits, main circuit main
module main (
);

  wire and_2_out, and_3_out, clas_12bit_1_c_out, not_2_out, not_3_out, xor_1_out, xor_2_out;
  wire [2:0] OpCode_sw3;
  wire [11:0] A_sw12, and_1_out, B_sw12, clas_12bit_1_result, multiplexer_1_out, not_1_out, or_1_out;

  DipSwitch #(.number(12)) B (
    .sw1(B_sw12[11]), .sw2(B_sw12[10]), .sw3(B_sw12[9]), .sw4(B_sw12[8]), .sw5(B_sw12[7]), .sw6(B_sw12[6]),
    .sw7(B_sw12[5]), .sw8(B_sw12[4]), .sw9(B_sw12[3]), .sw10(B_sw12[2]), .sw11(B_sw12[1]), .sw12(B_sw12[0]));
  DipSwitch #(.number(12)) A (
    .sw1(A_sw12[11]), .sw2(A_sw12[10]), .sw3(A_sw12[9]), .sw4(A_sw12[8]), .sw5(A_sw12[7]), .sw6(A_sw12[6]),
    .sw7(A_sw12[5]), .sw8(A_sw12[4]), .sw9(A_sw12[3]), .sw10(A_sw12[2]), .sw11(A_sw12[1]), .sw12(A_sw12[0]));
  assign and_1_out = B_sw12 & A_sw12;  // AND_Gate and_1, 12 bits wide
  assign or_1_out = B_sw12 | A_sw12;  // OR_Gate or_1, 12 bits wide
  assign not_1_out = ~A_sw12;  // NOT_Gate not_1, 12 bits wide
  CLAS_12bit clas_12bit_1 (
    .M(OpCode_sw3[0]), .A(A_sw12), .B(B_sw12), .c_out(clas_12bit_1_c_out), .result(clas_12bit_1_result));
  not not_2 (not_2_out, xor_1_out);
  ExactlyOne xor_1 (.out(xor_1_out), .in0(B_sw12[11]), .in1(OpCode_sw3[0]), .in2(A_sw12[11]));
  and and_2 (and_2_out, not_2_out, not_3_out, xor_2_out);
  xor xor_2 (xor_2_out, A_sw12[11], multiplexer_1_out[11]);
  not not_3 (not_3_out, OpCode_sw3[1]);
  LED V (.in(and_2_out));
  and and_3 (and_3_out, multiplexer_1_out[11], multiplexer_1_out[10], multiplexer_1_out[9], multiplexer_1_out[8], multiplexer_1_out[7], multiplexer_1_out[6], multiplexer_1_out[5], multiplexer_1_out[4], multiplexer_1_out[3], multiplexer_1_out[2], multiplexer_1_out[1], multiplexer_1_out[0]);
  Multiplexer #(.select(3), .width(12)) multiplexer_1 (
    .in0(clas_12bit_1_result), .in1(clas_12bit_1_result), .in2(and_1_out), .in3(or_1_out), .in4(not_1_out),
    .out(multiplexer_1_out), .sel(OpCode_sw3));  // open: in5, in6, in7
  DipSwitch #(.number(3)) OpCode (.sw1(OpCode_sw3[2]), .sw2(OpCode_sw3[1]), .sw3(OpCode_sw3[0]));
  LED Z (.in(and_3_out));
  LED C (.in(clas_12bit_1_c_out));
  LED N (.in(multiplexer_1_out[11]));
  LED led_1 (.in(multiplexer_1_out[11]));
  LED led_2 (.in(multiplexer_1_out[10]));
  LED led_3 (.in(multiplexer_1_out[9]));
  LED led_4 (.in(multiplexer_1_out[8]));
  LED led_5 (.in(multiplexer_1_out[7]));
  LED led_6 (.in(multiplexer_1_out[6]));
  LED led_7 (.in(multiplexer_1_out[5]));
  LED led_8 (.in(multiplexer_1_out[4]));
  LED led_9 (.in(multiplexer_1_out[3]));
  LED led_10 (.in(multiplexer_1_out[2]));
  LED led_11 (.in(multiplexer_1_out[1]));
  LED led_12 (.in(multiplexer_1_out[0]));

  // Notes on the sheet:
  //   B11
  //   A11
endmodule

module MUX_2to1 (
  input  S,
  input  A,
  input  B,
  output Y
);

  wire and_1_out, and_2_out, not_1_out;

  not not_1 (not_1_out, S);
  and and_1 (and_1_out, S, A);
  and and_2 (and_2_out, not_1_out, B);
  or or_1 (Y, and_1_out, and_2_out);
endmodule

module AND_4bit (
  input  [3:0] A,
  input  [3:0] B,
  output [3:0] Y
);

  and and_1 (Y[0], A[0], B[0]);
  and and_2 (Y[1], A[1], B[1]);
  and and_3 (Y[2], A[2], B[2]);
  and and_4 (Y[3], A[3], B[3]);

  // Notes on the sheet:
  //   A: pull=down
  //   B: pull=down
  //   Y: pull=down
endmodule

module BCD_7Seg (
  input  [3:0] in_1,
  output [6:0] out_2
);

  wire bcd_to_7_segment_decoder_1_p1, bcd_to_7_segment_decoder_1_p2, bcd_to_7_segment_decoder_1_p3,
       bcd_to_7_segment_decoder_1_p4, bcd_to_7_segment_decoder_1_p6, bcd_to_7_segment_decoder_1_p7,
       bcd_to_7_segment_decoder_1_p8, comparator_1_gt;

  // BCD_to_7_Segment_decoder bcd_to_7_segment_decoder_1: pin names not known; wires that end beside it: bcd_to_7_segment_decoder_1_p1, bcd_to_7_segment_decoder_1_p2, bcd_to_7_segment_decoder_1_p3, bcd_to_7_segment_decoder_1_p4, in_1, bcd_to_7_segment_decoder_1_p6, bcd_to_7_segment_decoder_1_p7, bcd_to_7_segment_decoder_1_p8
  Comparator #(.mode("unsigned"), .width(4)) comparator_1 (
    .a(in_1), .b(4'b1001), .gt(comparator_1_gt));  // open: eq, lt
  MUX_2to1 a (.S(comparator_1_gt), .A(1'b1), .B(bcd_to_7_segment_decoder_1_p6), .Y(out_2[0]));
  MUX_2to1 b (.S(comparator_1_gt), .A(1'b0), .B(bcd_to_7_segment_decoder_1_p8), .Y(out_2[1]));
  MUX_2to1 c (.S(comparator_1_gt), .A(1'b0), .B(bcd_to_7_segment_decoder_1_p7), .Y(out_2[2]));
  MUX_2to1 d (.S(comparator_1_gt), .A(1'b1), .B(bcd_to_7_segment_decoder_1_p4), .Y(out_2[3]));
  MUX_2to1 e (.S(comparator_1_gt), .A(1'b1), .B(bcd_to_7_segment_decoder_1_p2), .Y(out_2[4]));
  MUX_2to1 f (.S(comparator_1_gt), .A(1'b1), .B(bcd_to_7_segment_decoder_1_p3), .Y(out_2[5]));
  MUX_2to1 g (.S(comparator_1_gt), .A(1'b1), .B(bcd_to_7_segment_decoder_1_p1), .Y(out_2[6]));
  _7_Segment_Display u_7_segment_display_1 (
    .g(out_2[6]), .f(out_2[5]), .a(out_2[0]), .b(out_2[1]), .e(out_2[4]), .d(out_2[3]), .c(out_2[2]));  // open: dp

  // Notes on the sheet:
  //   out_2: pull=down
  //   in_1: pull=down
endmodule

module CLAS_4bit (
  input  M,
  input  c_in,
  input  [3:0] A,
  input  [3:0] B,
  output C_out,
  output out_6,
  output out_7,
  output \output ,
  output out_9
);

  wire and_1_out, and_2_out, and_3_out, and_4_out, and_5_out, and_6_out, and_7_out, and_8_out, and_9_out,
       and_10_out, B0_out, B1_out, B2_out, B3_out, c0_out, c1_out, c2_out, g0_out, g1_out, g2_out, g3_out,
       p0_out, p1_out, p2_out, p3_out;

  xor B3 (B3_out, B[3], M);
  xor B2 (B2_out, B[2], M);
  xor B1 (B1_out, B[1], M);
  xor B0 (B0_out, B[0], M);
  and g3 (g3_out, B3_out, A[3]);
  xor p3 (p3_out, B3_out, A[3]);
  and g2 (g2_out, B2_out, A[2]);
  xor p2 (p2_out, B2_out, A[2]);
  and g1 (g1_out, B1_out, A[1]);
  xor p1 (p1_out, B1_out, A[1]);
  and g0 (g0_out, B0_out, A[0]);
  xor p0 (p0_out, B0_out, A[0]);
  and and_1 (and_1_out, c_in, p0_out, p1_out, p2_out, p3_out);
  and and_2 (and_2_out, g0_out, p1_out, p2_out, p3_out);
  and and_3 (and_3_out, g1_out, p2_out, p3_out);
  and and_4 (and_4_out, g2_out, p3_out);
  and and_5 (and_5_out, p0_out, p1_out, p2_out, c_in);
  and and_6 (and_6_out, g0_out, p1_out, p2_out);
  and and_7 (and_7_out, p2_out, g1_out);
  and and_8 (and_8_out, c_in, p1_out, p0_out);
  and and_9 (and_9_out, g0_out, p1_out);
  and and_10 (and_10_out, c_in, p0_out);
  or c2 (c2_out, g2_out, and_5_out, and_6_out, and_7_out);
  or c1 (c1_out, g1_out, and_8_out, and_9_out);
  or c0 (c0_out, g0_out, and_10_out);
  or c3 (C_out, g3_out, and_1_out, and_2_out, and_3_out, and_4_out);
  xor s3 (out_6, p3_out, c2_out);
  xor s2 (out_7, p2_out, c1_out);
  xor s1 (\output , p1_out, c0_out);
  xor s0 (out_9, p0_out, c_in);

  // Notes on the sheet:
  //   A: pull=down
  //   B: pull=down
  //   M: pull=down
  //   c_in: pull=down
  //   C_out: pull=down
  //   out_6: pull=down
  //   out_7: pull=down
  //   output: pull=down
  //   out_9: pull=down
  //   c_in
endmodule

module CLAS_12bit (
  input  M,
  input  [11:0] A,
  input  [11:0] B,
  output c_out,
  output [11:0] result
);

  wire clas_4bit_1_c_out, clas_4bit_2_c_out;

  CLAS_4bit clas_4bit_1 (
    .M(M), .c_in(M), .A(A[3:0]), .B(B[3:0]), .C_out(clas_4bit_1_c_out), .out_6(result[3]), .out_7(result[2]),
    .\output (result[1]), .out_9(result[0]));
  CLAS_4bit clas_4bit_2 (
    .M(M), .c_in(clas_4bit_1_c_out), .A(A[7:4]), .B(B[7:4]), .C_out(clas_4bit_2_c_out), .out_6(result[7]),
    .out_7(result[6]), .\output (result[5]), .out_9(result[4]));
  CLAS_4bit clas_4bit_3 (
    .M(M), .c_in(clas_4bit_2_c_out), .A(A[11:8]), .B(B[11:8]), .C_out(c_out), .out_6(result[11]),
    .out_7(result[10]), .\output (result[9]), .out_9(result[8]));

  // Notes on the sheet:
  //   result: pull=down
  //   c_out: pull=down
  //   M: pull=down
  //   A: pull=down
  //   B: pull=down
  //   A0-A3/B0-B3
  //   A4-A7/B4-B7
  //   A8-A11/B8-B11
  //   2048 1024 512 256
  //   128 64 32 16
  //   8 4 2 1
endmodule
