// Logisim project HW4_4.circ as structural Verilog: 7 circuits, main circuit main
module main (
);

  wire alu_12bit_1_c, alu_12bit_1_n, alu_12bit_1_v, alu_12bit_1_z, CLK_out, decoder_1_out0, decoder_1_out1,
       decoder_1_out2, decoder_1_out3, decoder_1_out4, decoder_1_out5, decoder_1_out6, decoder_1_out7,
       WriteEn_p1;
  wire [2:0] undriven, undriven_2, undriven_3, undriven_4;
  wire [11:0] alu_12bit_1_sum, multiplexer_1_out, multiplexer_2_out, register_1_q, register_2_q,
       register_3_q, register_4_q, register_5_q, register_6_q, register_7_q, register_8_q;

  // DipSwitch #(.number(12)) dipswitch_1: pin names not known
  // DipSwitch #(.number(2)) WriteEn: pin names not known; wires that end beside it: WriteEn_p1
  LED led_1 (.in(undriven[2]));
  LED led_2 (.in(undriven[1]));
  LED led_3 (.in(undriven[0]));
  LED led_4 (.in(undriven_2[2]));
  LED led_5 (.in(undriven_2[1]));
  LED led_6 (.in(undriven_2[0]));
  Decoder #(.select(3)) decoder_1 (
    .out0(decoder_1_out0), .out1(decoder_1_out1), .out2(decoder_1_out2), .out3(decoder_1_out3),
    .out4(decoder_1_out4), .out5(decoder_1_out5), .out6(decoder_1_out6), .out7(decoder_1_out7),
    .sel(undriven_4), .en(WriteEn_p1));
  LED led_7 (.in(undriven_3[2]));
  LED led_8 (.in(undriven_3[1]));
  LED led_9 (.in(undriven_3[0]));
  LED led_10 (.in(undriven_4[2]));
  LED led_11 (.in(undriven_4[1]));
  LED led_12 (.in(undriven_4[0]));
  Register #(.width(12)) register_1 (
    .D(alu_12bit_1_sum), .en(decoder_1_out0), .clk(CLK_out), .Q(register_1_q));  // open: clr
  Register #(.width(12)) register_2 (
    .D(alu_12bit_1_sum), .en(decoder_1_out1), .clk(CLK_out), .Q(register_2_q));  // open: clr
  Register #(.width(12)) register_3 (
    .D(alu_12bit_1_sum), .en(decoder_1_out2), .clk(CLK_out), .Q(register_3_q));  // open: clr
  Register #(.width(12)) register_4 (
    .D(alu_12bit_1_sum), .en(decoder_1_out3), .clk(CLK_out), .Q(register_4_q));  // open: clr
  Register #(.width(12)) register_5 (
    .D(alu_12bit_1_sum), .en(decoder_1_out4), .clk(CLK_out), .Q(register_5_q));  // open: clr
  Register #(.width(12)) register_6 (
    .D(alu_12bit_1_sum), .en(decoder_1_out5), .clk(CLK_out), .Q(register_6_q));  // open: clr
  Register #(.width(12)) register_7 (
    .D(alu_12bit_1_sum), .en(decoder_1_out6), .clk(CLK_out), .Q(register_7_q));  // open: clr
  Register #(.width(12)) register_8 (
    .D(alu_12bit_1_sum), .en(decoder_1_out7), .clk(CLK_out), .Q(register_8_q));  // open: clr
  Clock CLK (.out(CLK_out));
  Multiplexer #(.select(3), .width(12)) multiplexer_1 (
    .in0(register_1_q), .in1(register_2_q), .in2(register_3_q), .in3(register_4_q), .in4(register_5_q),
    .in5(register_6_q), .in6(register_7_q), .in7(register_8_q), .out(multiplexer_1_out), .sel(undriven_2));
  Multiplexer #(.select(3), .width(12)) multiplexer_2 (
    .in0(register_1_q), .in1(register_2_q), .in2(register_3_q), .in3(register_4_q), .in4(register_5_q),
    .in5(register_6_q), .in6(register_7_q), .in7(register_8_q), .out(multiplexer_2_out), .sel(undriven_3));
  ALU_12bit alu_12bit_1 (
    .OpCode(undriven), .B(multiplexer_2_out), .A(multiplexer_1_out), .V(alu_12bit_1_v), .Z(alu_12bit_1_z),
    .C(alu_12bit_1_c), .N(alu_12bit_1_n), .Sum(alu_12bit_1_sum));
  LED V (.in(alu_12bit_1_v));
  LED Z (.in(alu_12bit_1_z));
  LED C (.in(alu_12bit_1_c));
  LED N (.in(alu_12bit_1_n));
  LED led_13 (.in(alu_12bit_1_sum[11]));
  LED led_14 (.in(alu_12bit_1_sum[10]));
  LED led_15 (.in(alu_12bit_1_sum[9]));
  LED led_16 (.in(alu_12bit_1_sum[8]));
  LED led_17 (.in(alu_12bit_1_sum[7]));
  LED led_18 (.in(alu_12bit_1_sum[6]));
  LED led_19 (.in(alu_12bit_1_sum[5]));
  LED led_20 (.in(alu_12bit_1_sum[4]));
  LED led_21 (.in(alu_12bit_1_sum[3]));
  LED led_22 (.in(alu_12bit_1_sum[2]));
  LED led_23 (.in(alu_12bit_1_sum[1]));
  LED led_24 (.in(alu_12bit_1_sum[0]));

  // Notes on the sheet:
  //   OP
  //   RM
  //   RN
  //   RD
  //   OP
  //   RM
  //   RN
  //   RD
  //   000
  //   001
  //   010
  //   011
  //   100
  //   101
  //   110
  //   111
  //   WD
  //   RM
  //   RN
  //   Sum
endmodule

module MUX_2to1 (
  input  S,
  input  A,
  input  B,
  output Y
);

  wire and_1_out, and_2_out, not_1_out;

  not not_1 (not_1_out, S);
  and and_1 (and_1_out, S, A);
  and and_2 (and_2_out, not_1_out, B);
  or or_1 (Y, and_1_out, and_2_out);
endmodule

module AND_4bit (
  input  [3:0] A,
  input  [3:0] B,
  output [3:0] Y
);

  and and_1 (Y[0], A[0], B[0]);
  and and_2 (Y[1], A[1], B[1]);
  and and_3 (Y[2], A[2], B[2]);
  and and_4 (Y[3], A[3], B[3]);

  // Notes on the sheet:
  //   A: pull=down
  //   B: pull=down
  //   Y: pull=down
endmodule

module BCD_7Seg (
  input  [3:0] in_1,
  output [6:0] out_2
);

  wire bcd_to_7_segment_decoder_1_p1, bcd_to_7_segment_decoder_1_p2, bcd_to_7_segment_decoder_1_p3,
       bcd_to_7_segment_decoder_1_p4, bcd_to_7_segment_decoder_1_p6, bcd_to_7_segment_decoder_1_p7,
       bcd_to_7_segment_decoder_1_p8, comparator_1_gt;

  // BCD_to_7_Segment_decoder bcd_to_7_segment_decoder_1: pin names not known; wires that end beside it: bcd_to_7_segment_decoder_1_p1, bcd_to_7_segment_decoder_1_p2, bcd_to_7_segment_decoder_1_p3, bcd_to_7_segment_decoder_1_p4, in_1, bcd_to_7_segment_decoder_1_p6, bcd_to_7_segment_decoder_1_p7, bcd_to_7_segment_decoder_1_p8
  Comparator #(.mode("unsigned"), .width(4)) comparator_1 (
    .a(in_1), .b(4'b1001), .gt(comparator_1_gt));  // open: eq, lt
  MUX_2to1 a (.S(comparator_1_gt), .A(1'b1), .B(bcd_to_7_segment_decoder_1_p6), .Y(out_2[0]));
  MUX_2to1 b (.S(comparator_1_gt), .A(1'b0), .B(bcd_to_7_segment_decoder_1_p8), .Y(out_2[1]));
  MUX_2to1 c (.S(comparator_1_gt), .A(1'b0), .B(bcd_to_7_segment_decoder_1_p7), .Y(out_2[2]));
  MUX_2to1 d (.S(comparator_1_gt), .A(1'b1), .B(bcd_to_7_segment_decoder_1_p4), .Y(out_2[3]));
  MUX_2to1 e (.S(comparator_1_gt), .A(1'b1), .B(bcd_to_7_segment_decoder_1_p2), .Y(out_2[4]));
  MUX_2to1 f (.S(comparator_1_gt), .A(1'b1), .B(bcd_to_7_segment_decoder_1_p3), .Y(out_2[5]));
  MUX_2to1 g (.S(comparator_1_gt), .A(1'b1), .B(bcd_to_7_segment_decoder_1_p1), .Y(out_2[6]));
  _7_Segment_Display u_7_segment_display_1 (
    .g(out_2[6]), .f(out_2[5]), .a(out_2[0]), .b(out_2[1]), .e(out_2[4]), .d(out_2[3]), .c(out_2[2]));  // open: dp

  // Notes on the sheet:
  //   out_2: pull=down
  //   in_1: pull=down
endmodule

module CLAS_4bit (
  input  M,
  input  c_in,
  input  [3:0] A,
  input  [3:0] B,
  output C_out,
  output out_6,
  output out_7,
  output \output ,
  output out_9
);

  wire and_1_out, and_2_out, and_3_out, and_4_out, and_5_out, and_6_out, and_7_out, and_8_out, and_9_out,
       and_10_out, B0_out, B1_out, B2_out, B3_out, c0_out, c1_out, c2_out, g0_out, g1_out, g2_out, g3_out,
       p0_out, p1_out, p2_out, p3_out;

  xor B3 (B3_out, B[3], M);
  xor B2 (B2_out, B[2], M);
  xor B1 (B1_out, B[1], M);
  xor B0 (B0_out, B[0], M);
  and g3 (g3_out, B3_out, A[3]);
  xor p3 (p3_out, B3_out, A[3]);
  and g2 (g2_out, B2_out, A[2]);
  xor p2 (p2_out, B2_out, A[2]);
  and g1 (g1_out, B1_out, A[1]);
  xor p1 (p1_out, B1_out, A[1]);
  and g0 (g0_out, B0_out, A[0]);
  xor p0 (p0_out, B0_out, A[0]);
  and and_1 (and_1_out, c_in, p0_out, p1_out, p2_out, p3_out);
  and and_2 (and_2_out, g0_out, p1_out, p2_out, p3_out);
  and and_3 (and_3_out, g1_out, p2_out, p3_out);
  and and_4 (and_4_out, g2_out, p3_out);
  and and_5 (and_5_out, p0_out, p1_out, p2_out, c_in);
  and and_6 (and_6_out, g0_out, p1_out, p2_out);
  and and_7 (and_7_out, p2_out, g1_out);
  and and_8 (and_8_out, c_in, p1_out, p0_out);
  and and_9 (and_9_out, g0_out, p1_out);
  and and_10 (and_10_out, c_in, p0_out);
  or c2 (c2_out, g2_out, and_5_out, and_6_out, and_7_out);
  or c1 (c1_out, g1_out, and_8_out, and_9_out);
  or c0 (c0_out, g0_out, and_10_out);
  or c3 (C_out, g3_out, and_1_out, and_2_out, and_3_out, and_4_out);
  xor s3 (out_6, p3_out, c2_out);
  xor s2 (out_7, p2_out, c1_out);
  xor s1 (\output , p1_out, c0_out);
  xor s0 (out_9, p0_out, c_in);

  // Notes on the sheet:
  //   A: pull=down
  //   B: pull=down
  //   M: pull=down
  //   c_in: pull=down
  //   C_out: pull=down
  //   out_6: pull=down
  //   out_7: pull=down
  //   output: pull=down
  //   out_9: pull=down
  //   c_in
endmodule

module CLAS_12bit (
  input  M,
  input  [11:0] A,
  input  [11:0] B,
  output c_out,
  output [11:0] result
);

  wire clas_4bit_1_c_out, clas_4bit_2_c_out;

  CLAS_4bit clas_4bit_1 (
    .M(M), .c_in(M), .A(A[3:0]), .B(B[3:0]), .C_out(clas_4bit_1_c_out), .out_6(result[3]), .out_7(result[2]),
    .\output (result[1]), .out_9(result[0]));
  CLAS_4bit clas_4bit_2 (
    .M(M), .c_in(clas_4bit_1_c_out), .A(A[7:4]), .B(B[7:4]), .C_out(clas_4bit_2_c_out), .out_6(result[7]),
    .out_7(result[6]), .\output (result[5]), .out_9(result[4]));
  CLAS_4bit clas_4bit_3 (
    .M(M), .c_in(clas_4bit_2_c_out), .A(A[11:8]), .B(B[11:8]), .C_out(c_out), .out_6(result[11]),
    .out_7(result[10]), .\output (result[9]), .out_9(result[8]));

  // Notes on the sheet:
  //   result: pull=down
  //   c_out: pull=down
  //   M: pull=down
  //   A: pull=down
  //   B: pull=down
  //   A0-A3/B0-B3
  //   A4-A7/B4-B7
  //   A8-A11/B8-B11
  //   2048 1024 512 256
  //   128 64 32 16
  //   8 4 2 1
endmodule

module ALU_12bit (
  input  [2:0] OpCode,
  input  [11:0] B,
  input  [11:0] A,
  output V,
  output Z,
  output C,
  output N,
  output [11:0] Sum
);

  wire not_2_out, not_3_out, xor_1_out, xor_2_out;
  wire [11:0] and_1_out, clas_12bit_1_result, not_1_out, or_1_out;

  assign and_1_out = B & A;  // AND_Gate and_1, 12 bits wide
  assign or_1_out = B | A;  // OR_Gate or_1, 12 bits wide
  assign not_1_out = ~A;  // NOT_Gate not_1, 12 bits wide
  CLAS_12bit clas_12bit_1 (.M(OpCode[0]), .A(A), .B(B), .c_out(C), .result(clas_12bit_1_result));
  not not_2 (not_2_out, xor_1_out);
  ExactlyOne xor_1 (.out(xor_1_out), .in0(B[11]), .in1(OpCode[0]), .in2(A[11]));
  and and_2 (V, not_2_out, not_3_out, xor_2_out);
  xor xor_2 (xor_2_out, A[11], N);
  not not_3 (not_3_out, OpCode[1]);
  and and_3 (Z, N, Sum[10], Sum[9], Sum[8], Sum[7], Sum[6], Sum[5], Sum[4], Sum[3], Sum[2], Sum[1], Sum[0]);
  Multiplexer #(.select(3), .width(12)) multiplexer_1 (
    .in0(clas_12bit_1_result), .in1(clas_12bit_1_result), .in2(and_1_out), .in3(or_1_out), .in4(not_1_out),
    .out({N, Sum[10:0]}), .sel(OpCode));  // open: in5, in6, in7
  LED led_1 (.in(N));
  LED led_2 (.in(Sum[10]));
  LED led_3 (.in(Sum[9]));
  LED led_4 (.in(Sum[8]));
  LED led_5 (.in(Sum[7]));
  LED led_6 (.in(Sum[6]));
  LED led_7 (.in(Sum[5]));
  LED led_8 (.in(Sum[4]));
  LED led_9 (.in(Sum[3]));
  LED led_10 (.in(Sum[2]));
  LED led_11 (.in(Sum[1]));
  LED led_12 (.in(Sum[0]));

  assign Sum[11] = N;

  // Notes on the sheet:
  //   B: pull=down
  //   A: pull=down
  //   OpCode: pull=down
  //   V: pull=down
  //   Z: pull=down
  //   C: pull=down
  //   N: pull=down
  //   Sum: pull=down
  //   B11
  //   A11
endmodule
